// Digital circuit AddSub1b.dig as structural Verilog
module AddSub1b (
  input  A,
  input  B,
  input  Ctrl,
  input  Ci,
  output S,
  output Co
);

  wire xor_1_out;

  xor xor_1 (xor_1_out, B, Ctrl);
  Adder1b adder1b_1 (.A(A), .B(xor_1_out), .C(Ci), .S(S), .Co(Co));
endmodule
