// Digital circuit AddSub4b.dig as structural Verilog
module AddSub4b (
  input  Ctrl,
  input  [3:0] A,
  input  [3:0] B,
  output [3:0] S,
  output Co
);

  wire addsub1b_1_co, addsub1b_2_co, addsub1b_3_co;

  AddSub1b addsub1b_1 (.A(A[0]), .B(B[0]), .Ctrl(Ctrl), .Ci(Ctrl), .S(S[0]), .Co(addsub1b_1_co));
  AddSub1b addsub1b_2 (.A(A[1]), .B(B[1]), .Ctrl(Ctrl), .Ci(addsub1b_1_co), .S(S[1]), .Co(addsub1b_2_co));
  AddSub1b addsub1b_3 (.A(A[2]), .B(B[2]), .Ctrl(Ctrl), .Ci(addsub1b_2_co), .S(S[2]), .Co(addsub1b_3_co));
  AddSub1b addsub1b_4 (.A(A[3]), .B(B[3]), .Ctrl(Ctrl), .Ci(addsub1b_3_co), .S(S[3]), .Co(Co));
endmodule
