// Digital circuit Adder1b.dig as structural Verilog
module Adder1b (
  input  A,
  input  B,
  input  C,
  output S,
  output Co
);

  wire and_1_out, and_2_out, and_3_out, xor_1_out;

  xor xor_1 (xor_1_out, A, B);
  and and_1 (and_1_out, A, B);
  and and_2 (and_2_out, A, C);
  and and_3 (and_3_out, B, C);
  xor xor_2 (S, xor_1_out, C);
  or or_1 (Co, and_1_out, and_2_out, and_3_out);
endmodule
