// Digital circuit D_Latch.dig as structural Verilog
module D_Latch (
  input  D,
  input  C,
  output Q,
  output Q_bar
);

  wire nand_1_out, nand_2_out, not_1_out;

  not not_1 (not_1_out, D);
  nand nand_1 (nand_1_out, D, C);
  nand nand_2 (nand_2_out, C, not_1_out);
  nand nand_3 (Q, nand_1_out, Q_bar);
  nand nand_4 (Q_bar, Q, nand_2_out);
endmodule
