// Digital circuit DispNum.dig as structural Verilog
module DispNum (
  input  [1:0] scan,
  input  [15:0] HEXS,
  input  [3:0] point,
  input  [3:0] LES,
  output [3:0] AN,
  output [7:0] SEGMENT
);

  wire decoder_1_out_0, decoder_1_out_1, decoder_1_out_2, decoder_1_out_3, mux4to1_1_o, mux4to1_2_o;
  wire [3:0] mux4to1b4_1_o;

  Decoder #(.Selector_Bits(2)) decoder_1 (
    .sel(scan), .out_0(decoder_1_out_0), .out_1(decoder_1_out_1), .out_2(decoder_1_out_2),
    .out_3(decoder_1_out_3));
  Mux4to1 mux4to1_1 (.S(scan), .I(point), .O(mux4to1_1_o));
  Mux4to1 mux4to1_2 (.S(scan), .I(LES), .O(mux4to1_2_o));
  not not_1 (AN[0], decoder_1_out_0);
  not not_2 (AN[1], decoder_1_out_1);
  not not_3 (AN[2], decoder_1_out_2);
  not not_4 (AN[3], decoder_1_out_3);
  Mux4to1b4 mux4to1b4_1 (
    .I0(HEXS[3:0]), .I1(HEXS[7:4]), .I2(HEXS[11:8]), .I3(HEXS[15:12]), .S(scan), .O(mux4to1b4_1_o));
  MyMC14495 mymc14495_1 (
    .point(mux4to1_1_o), .LE(mux4to1_2_o), .D0(mux4to1b4_1_o[0]), .D1(mux4to1b4_1_o[1]),
    .D2(mux4to1b4_1_o[2]), .D3(mux4to1b4_1_o[3]), .g(SEGMENT[6]), .f(SEGMENT[5]), .e(SEGMENT[4]),
    .d(SEGMENT[3]), .c(SEGMENT[2]), .b(SEGMENT[1]), .a(SEGMENT[0]), .p(SEGMENT[7]));
endmodule
