// Digital circuit DispNum_Test.dig as structural Verilog
module DispNum_Test (
  input  clk
);

  wire not_1_out, not_2_out, not_3_out, not_4_out;
  wire [1:0] counter_1_out;
  wire [3:0] dispnum_1_an;
  wire [7:0] dispnum_1_segment;

  Counter #(.Bits(2)) counter_1 (.en(1'b1), .C(clk), .clr(1'b0), .out(counter_1_out));  // open: ovf
  DispNum dispnum_1 (
    .scan(counter_1_out), .HEXS(16'habcd), .point(4'b0001), .LES(4'b0000), .AN(dispnum_1_an),
    .SEGMENT(dispnum_1_segment));
  not not_1 (not_1_out, dispnum_1_an[0]);
  not not_2 (not_2_out, dispnum_1_an[1]);
  not not_3 (not_3_out, dispnum_1_an[2]);
  not not_4 (not_4_out, dispnum_1_an[3]);
  Seven_Seg #(.commonCathode("true"), .commonConnectionType("anode")) seven_seg_1 (
    .a(dispnum_1_segment[0]), .b(dispnum_1_segment[1]), .c(dispnum_1_segment[2]), .d(dispnum_1_segment[3]),
    .e(dispnum_1_segment[4]), .f(dispnum_1_segment[5]), .g(dispnum_1_segment[6]), .dp(dispnum_1_segment[7]),
    .common(not_4_out));
  Seven_Seg #(.commonCathode("true"), .commonConnectionType("anode")) seven_seg_2 (
    .a(dispnum_1_segment[0]), .b(dispnum_1_segment[1]), .c(dispnum_1_segment[2]), .d(dispnum_1_segment[3]),
    .e(dispnum_1_segment[4]), .f(dispnum_1_segment[5]), .g(dispnum_1_segment[6]), .dp(dispnum_1_segment[7]),
    .common(not_3_out));
  Seven_Seg #(.commonCathode("true"), .commonConnectionType("anode")) seven_seg_3 (
    .a(dispnum_1_segment[0]), .b(dispnum_1_segment[1]), .c(dispnum_1_segment[2]), .d(dispnum_1_segment[3]),
    .e(dispnum_1_segment[4]), .f(dispnum_1_segment[5]), .g(dispnum_1_segment[6]), .dp(dispnum_1_segment[7]),
    .common(not_2_out));
  Seven_Seg #(.commonCathode("true"), .commonConnectionType("anode")) seven_seg_4 (
    .a(dispnum_1_segment[0]), .b(dispnum_1_segment[1]), .c(dispnum_1_segment[2]), .d(dispnum_1_segment[3]),
    .e(dispnum_1_segment[4]), .f(dispnum_1_segment[5]), .g(dispnum_1_segment[6]), .dp(dispnum_1_segment[7]),
    .common(not_1_out));
endmodule
