// Digital circuit Gated_SR_Latch.dig as structural Verilog
module Gated_SR_Latch (
  input  R,
  input  S,
  output Q,
  output Q_bar
);

  nand nand_1 (Q, R, Q_bar);
  nand nand_2 (Q_bar, Q, S);
endmodule
