// Digital circuit LampCtrl138.dig as structural Verilog
module LampCtrl138 (
  input  S1,
  input  S2,
  input  S3,
  output F
);

  wire [7:0] d_74ls138_1_y;

  D_74LS138 d_74ls138_1 (.C(S1), .B(S2), .A(S3), .G(1'b1), .G2A(1'b0), .G2B(1'b0), .Y(d_74ls138_1_y));
  nand nand_1 (F, d_74ls138_1_y[1], d_74ls138_1_y[2], d_74ls138_1_y[4], d_74ls138_1_y[7]);
endmodule
