// Digital circuit Lampctrl_sch.dig as structural Verilog
module Lampctrl_sch (
  input  S1,
  input  S2,
  input  S3,
  output F
);

  wire and_1_out, and_2_out, and_3_out, and_4_out, not_1_out, not_2_out, not_3_out;

  not not_1 (not_1_out, S1);
  not not_2 (not_2_out, S2);
  not not_3 (not_3_out, S3);
  and and_1 (and_1_out, S1, not_2_out, not_3_out);
  and and_2 (and_2_out, not_1_out, S2, not_3_out);
  and and_3 (and_3_out, not_1_out, not_2_out, S3);
  and and_4 (and_4_out, S1, S2, S3);
  or or_1 (F, and_1_out, and_2_out, and_3_out, and_4_out);
endmodule
