// Digital circuit MS_SR_FlipFlop.dig as structural Verilog
module MS_SR_FlipFlop (
  input  S,
  input  C,
  input  R,
  output Q,
  output Q_bar
);

  wire not_1_out, real_gated_sr_latch_1_q, real_gated_sr_latch_1_q_bar;

  Real_Gated_SR_Latch real_gated_sr_latch_1 (
    .R(R), .S(S), .C(C), .Q(real_gated_sr_latch_1_q), .Q_bar(real_gated_sr_latch_1_q_bar));
  not not_1 (not_1_out, C);
  Real_Gated_SR_Latch real_gated_sr_latch_2 (
    .R(real_gated_sr_latch_1_q_bar), .S(real_gated_sr_latch_1_q), .C(not_1_out), .Q(Q), .Q_bar(Q_bar));
endmodule
