// Digital circuit Mux4to1b4.dig as structural Verilog
module Mux4to1b4 (
  input  [3:0] I0,
  input  [3:0] I1,
  input  [3:0] I2,
  input  [3:0] I3,
  input  [1:0] S,
  output [3:0] O
);

  wire and_1_out, and_2_out, and_3_out, and_4_out, and_5_out, and_6_out, and_7_out, and_8_out, and_9_out,
       and_10_out, and_11_out, and_12_out, and_13_out, and_14_out, and_15_out, and_16_out, and_17_out,
       and_18_out, and_19_out, and_20_out, not_1_out, not_2_out;

  not not_1 (not_1_out, S[0]);
  not not_2 (not_2_out, S[1]);
  and and_1 (and_1_out, not_1_out, not_2_out);
  and and_2 (and_2_out, S[0], not_2_out);
  and and_3 (and_3_out, not_1_out, S[1]);
  and and_4 (and_4_out, S[1], S[0]);
  and and_5 (and_5_out, and_1_out, I0[0]);
  and and_6 (and_6_out, and_2_out, I1[0]);
  and and_7 (and_7_out, and_3_out, I2[0]);
  and and_8 (and_8_out, and_4_out, I3[0]);
  and and_9 (and_9_out, and_1_out, I0[1]);
  and and_10 (and_10_out, and_2_out, I1[1]);
  and and_11 (and_11_out, and_3_out, I2[1]);
  and and_12 (and_12_out, and_4_out, I3[1]);
  and and_13 (and_13_out, and_1_out, I0[2]);
  and and_14 (and_14_out, and_2_out, I1[2]);
  and and_15 (and_15_out, and_3_out, I2[2]);
  and and_16 (and_16_out, and_4_out, I3[2]);
  and and_17 (and_17_out, and_1_out, I0[3]);
  and and_18 (and_18_out, and_2_out, I1[3]);
  and and_19 (and_19_out, and_3_out, I2[3]);
  and and_20 (and_20_out, and_4_out, I3[3]);
  or or_1 (O[0], and_5_out, and_6_out, and_7_out, and_8_out);
  or or_2 (O[1], and_9_out, and_10_out, and_11_out, and_12_out);
  or or_3 (O[2], and_13_out, and_14_out, and_15_out, and_16_out);
  or or_4 (O[3], and_17_out, and_18_out, and_19_out, and_20_out);

  // Other names for the same wires on the sheet: _100 = I0[0]; _101 = I0[1]; _102 = I0[2]; _103 = I0[3]; _110 = I1[0];
  //   _111 = I1[1]; _112 = I1[2]; _113 = I1[3]; _120 = I2[0]; _121 = I2[1]; _122 = I2[2]; _123 = I2[3]; _130 = I3[0];
  //   _131 = I3[1]; _132 = I3[2]; _133 = I3[3]
endmodule
