// Digital circuit Real_Gated_SR_Latch.dig as structural Verilog
module Real_Gated_SR_Latch (
  input  R,
  input  S,
  input  C,
  output Q,
  output Q_bar
);

  wire nand_1_out, nand_2_out;

  nand nand_1 (nand_1_out, S, C);
  nand nand_2 (nand_2_out, C, R);
  nand nand_3 (Q, nand_1_out, Q_bar);
  nand nand_4 (Q_bar, Q, nand_2_out);
endmodule
