// Digital circuit Adder4b.dig as structural Verilog
module Adder4b (
  input  Ci,
  input  [3:0] A,
  input  [3:0] B,
  output [3:0] S,
  output Co
);

  wire adder1b_1_co, adder1b_2_co, adder1b_3_co;

  Adder1b adder1b_1 (.A(A[0]), .B(B[0]), .C(Ci), .S(S[0]), .Co(adder1b_1_co));
  Adder1b adder1b_2 (.A(A[1]), .B(B[1]), .C(adder1b_1_co), .S(S[1]), .Co(adder1b_2_co));
  Adder1b adder1b_3 (.A(A[2]), .B(B[2]), .C(adder1b_2_co), .S(S[2]), .Co(adder1b_3_co));
  Adder1b adder1b_4 (.A(A[3]), .B(B[3]), .C(adder1b_3_co), .S(S[3]), .Co(Co));
endmodule
