// Digital circuit MyMC14495.dig as structural Verilog
module MyMC14495 (
  input  point,
  input  LE,
  input  D0,
  input  D1,
  input  D2,
  input  D3,
  output g,
  output f,
  output e,
  output d,
  output c,
  output b,
  output a,
  output p
);

  wire and_1_out, and_2_out, and_3_out, and_4_out, and_5_out, and_6_out, and_7_out, and_8_out, and_9_out,
       and_10_out, and_11_out, and_12_out, and_13_out, and_14_out, and_15_out, and_16_out, and_17_out,
       and_18_out, and_19_out, and_20_out, and_21_out, and_22_out, and_23_out, and_24_out, and_25_out,
       not_2_out, not_3_out, not_4_out, not_5_out, or_1_out, or_3_out, or_5_out, or_7_out, or_11_out,
       or_13_out, or_14_out;

  not not_1 (p, point);
  and and_1 (and_1_out, not_4_out, not_3_out, not_2_out);
  and and_2 (and_2_out, D0, D1, D2, not_2_out);
  or or_1 (or_1_out, and_3_out, and_2_out, and_1_out);
  and and_3 (and_3_out, not_5_out, not_4_out, D2, D3);
  and and_4 (and_4_out, D0, not_3_out, not_2_out);
  or or_2 (g, or_1_out, LE);
  and and_5 (and_5_out, D1, not_3_out, not_2_out);
  and and_6 (and_6_out, D0, D1, not_2_out);
  or or_3 (or_3_out, and_7_out, and_6_out, and_5_out, and_4_out);
  or or_4 (f, or_3_out, LE);
  and and_7 (and_7_out, D0, not_4_out, D2, D3);
  and and_8 (and_8_out, D0, not_2_out);
  or or_5 (or_5_out, and_10_out, and_9_out, and_8_out);
  and and_9 (and_9_out, not_4_out, D2, not_2_out);
  and and_10 (and_10_out, D0, not_4_out, not_3_out);
  or or_6 (e, or_5_out, LE);
  and and_11 (and_11_out, D0, not_4_out, not_3_out, not_2_out);
  or or_7 (or_7_out, and_14_out, and_13_out, and_12_out, and_11_out);
  or or_8 (d, or_7_out, LE);
  and and_12 (and_12_out, not_5_out, not_4_out, D2, not_2_out);
  and and_13 (and_13_out, D0, D1, D2);
  or or_9 (c, or_11_out, LE);
  and and_14 (and_14_out, not_5_out, D1, not_3_out, D3);
  or or_10 (b, or_13_out, LE);
  and and_15 (and_15_out, not_5_out, D1, not_3_out, not_2_out);
  or or_11 (or_11_out, and_17_out, and_16_out, and_15_out);
  or or_12 (a, or_14_out, LE);
  and and_16 (and_16_out, not_5_out, D2, D3);
  and and_17 (and_17_out, D1, D2, D3);
  and and_18 (and_18_out, D0, not_4_out, D2, not_2_out);
  or or_13 (or_13_out, and_21_out, and_20_out, and_19_out, and_18_out);
  and and_19 (and_19_out, not_5_out, D1, D2);
  and and_20 (and_20_out, not_5_out, D2, D3);
  and and_21 (and_21_out, D0, D1, D3);
  and and_22 (and_22_out, D0, not_4_out, not_3_out, not_2_out);
  and and_23 (and_23_out, not_5_out, not_4_out, D2, not_2_out);
  or or_14 (or_14_out, and_25_out, and_24_out, and_23_out, and_22_out);
  and and_24 (and_24_out, D0, D1, not_3_out, D3);
  and and_25 (and_25_out, D0, not_4_out, D2, D3);
  not not_2 (not_2_out, D3);
  not not_3 (not_3_out, D2);
  not not_4 (not_4_out, D1);
  not not_5 (not_5_out, D0);
endmodule

/* Test case:
D3 D2 D1 D0 point LE a b c d e f g p
0 0 0 0 0 0 x x x x x x x x
0 0 0 1 0 0 x x x x x x x x
0 0 1 0 0 0 x x x x x x x x
0 0 1 1 0 0 x x x x x x x x
0 1 0 0 0 0 x x x x x x x x
0 1 0 1 0 0 x x x x x x x x
0 1 1 0 0 0 x x x x x x x x
0 1 1 1 0 0 x x x x x x x x
1 0 0 0 0 0 x x x x x x x x
1 0 0 1 0 0 x x x x x x x x
1 0 1 0 0 0 x x x x x x x x
1 0 1 1 0 0 x x x x x x x x
1 1 0 0 0 0 x x x x x x x x
1 1 0 1 0 0 x x x x x x x x
1 1 1 0 0 0 x x x x x x x x
1 1 1 1 0 0 x x x x x x x x
0 0 0 0 0 1 x x x x x x x x
0 0 0 1 1 0 x x x x x x x x
*/
