// Digital circuit MyMC14495_Test.dig as structural Verilog
module MyMC14495_Test (
  input  B,
  input  C,
  input  D,
  input  P,
  input  LE,
  input  A
);

  wire mymc14495_1_a, mymc14495_1_b, mymc14495_1_c, mymc14495_1_d, mymc14495_1_e, mymc14495_1_f,
       mymc14495_1_g, mymc14495_1_p;

  MyMC14495 mymc14495_1 (
    .point(P), .LE(LE), .D0(D), .D1(C), .D2(B), .D3(A), .g(mymc14495_1_g), .f(mymc14495_1_f),
    .e(mymc14495_1_e), .d(mymc14495_1_d), .c(mymc14495_1_c), .b(mymc14495_1_b), .a(mymc14495_1_a),
    .p(mymc14495_1_p));
  Seven_Seg #(.commonCathode("true"), .commonConnectionType("anode")) seven_seg_1 (
    .a(mymc14495_1_a), .b(mymc14495_1_b), .c(mymc14495_1_c), .d(mymc14495_1_d), .e(mymc14495_1_e),
    .f(mymc14495_1_f), .g(mymc14495_1_g), .dp(mymc14495_1_p), .common(1'b1));
endmodule
