// Digital circuit Counter4b.dig as structural Verilog
module Counter4b (
  input  clk,
  output RC,
  output QA,
  output QB,
  output QC,
  output QD
);

  wire and_2_out, and_3_out, d_ff_4_nq, xor_1_out, xor_2_out, xor_3_out;

  and and_1 (RC, QD, QC, QB, QA);
  and and_2 (and_2_out, QB, QC, QD);
  and and_3 (and_3_out, QC, QD);
  xor xor_1 (xor_1_out, QA, and_2_out);
  xor xor_2 (xor_2_out, QB, and_3_out);
  xor xor_3 (xor_3_out, QC, QD);
  D_FF d_ff_1 (.D(xor_1_out), .C(clk), .Q(QA));  // open: nQ
  D_FF d_ff_2 (.D(xor_2_out), .C(clk), .Q(QB));  // open: nQ
  D_FF d_ff_3 (.D(xor_3_out), .C(clk), .Q(QC));  // open: nQ
  D_FF d_ff_4 (.D(d_ff_4_nq), .C(clk), .Q(QD), .nQ(d_ff_4_nq));
endmodule
