// Digital circuit D_FlipFlop.dig as structural Verilog
module D_FlipFlop (
  input  D,
  input  C_p,
  input  S_bar,
  input  R_bar,
  output Q,
  output Q_bar
);

  wire nand_1_out, nand_2_out, nand_3_out, nand_4_out;

  nand nand_1 (nand_1_out, S_bar, nand_4_out, nand_2_out);
  nand nand_2 (nand_2_out, nand_1_out, R_bar, C_p);
  nand nand_3 (nand_3_out, nand_2_out, C_p, nand_4_out);
  nand nand_4 (nand_4_out, nand_3_out, D, R_bar);
  nand nand_5 (Q, S_bar, nand_2_out, Q_bar);
  nand nand_6 (Q_bar, Q, nand_3_out, R_bar);
endmodule
