// Digital circuit D_Latch_Flip.dig as structural Verilog
module D_Latch_Flip (
  input  EN,
  input  C,
  output Q,
  output Q_bar
);

  wire and_1_out;

  and and_1 (and_1_out, Q_bar, EN);
  D_Latch d_latch_1 (.D(and_1_out), .C(C), .Q(Q), .Q_bar(Q_bar));
endmodule
