// Digital circuit Mux4to1.dig as structural Verilog
module Mux4to1 (
  input  [1:0] S,
  input  [3:0] I,
  output O
);

  wire and_1_out, and_2_out, and_3_out, and_4_out, and_5_out, and_6_out, and_7_out, and_8_out, not_1_out,
       not_2_out;

  not not_1 (not_1_out, S[0]);
  not not_2 (not_2_out, S[1]);
  and and_1 (and_1_out, not_1_out, not_2_out);
  and and_2 (and_2_out, S[0], not_2_out);
  and and_3 (and_3_out, not_1_out, S[1]);
  and and_4 (and_4_out, S[1], S[0]);
  and and_5 (and_5_out, and_1_out, I[0]);
  and and_6 (and_6_out, and_2_out, I[1]);
  and and_7 (and_7_out, and_3_out, I[2]);
  and and_8 (and_8_out, and_4_out, I[3]);
  or or_1 (O, and_5_out, and_6_out, and_7_out, and_8_out);
endmodule

/* Test case:
S1	S0	I0	I1	I2	I3	O
0	0	0	1	0	1	0
0	1	0	1	0	1	1
1	0	0	1	0	1	0
1	1	0	1	0	1	1
*/
