// Digital circuit MyALU.dig as structural Verilog
module MyALU (
  input  [1:0] S,
  input  [3:0] A,
  input  [3:0] B,
  output Co,
  output [3:0] C
);

  wire [1:1] addsub4b_1_co;
  wire [3:0] addsub4b_1_s, and_1_out, or_1_out;

  AddSub4b addsub4b_1 (.Ctrl(S[0]), .A(A), .B(B), .S(addsub4b_1_s), .Co(addsub4b_1_co[1]));
  assign and_1_out = A & B;  // And and_1, 4 bits wide
  assign or_1_out = A | B;  // Or or_1, 4 bits wide
  Mux4to1b4 mux4to1b4_1 (.I0(addsub4b_1_s), .I1(addsub4b_1_s), .I2(and_1_out), .I3(or_1_out), .S(S), .O(C));
  Mux4to1 mux4to1_1 (.S(S), .I({2'b00, {2{addsub4b_1_co[1]}}}), .O(Co));
endmodule
